// Digital circuit Ejercicio3a.dig as structural Verilog
module Ejercicio3a (
  input  Set,
  input  Reset,
  input  Clock,
  output Q,
  output Q_2
);

  wire nand_1_out, nand_2_out, nand_3_out, nand_4_out, nand_5_out, nand_6_out, not_1_out;

  not not_1 (not_1_out, Clock);
  nand nand_1 (nand_1_out, Set, not_1_out);
  nand nand_2 (nand_2_out, not_1_out, Reset);
  nand nand_3 (nand_3_out, nand_1_out, nand_4_out);
  nand nand_4 (nand_4_out, nand_3_out, nand_2_out);
  nand nand_5 (nand_5_out, nand_3_out, Clock);
  nand nand_6 (nand_6_out, Clock, nand_4_out);
  nand nand_7 (Q, nand_5_out, Q_2);
  nand nand_8 (Q_2, Q, nand_6_out);

  // Notes on the sheet:
  //   Este circuito basicamente permite asignar el valor de 1 logico a un dato Q al activar 
  //   una entrada denominada 'SET' y devolverlo al 0 logico al activar una entrada 
  //   denominada 'Clear', es decir, podemos enviar el bit o grupo de bit a a un valor 
  //   conocido (0 o 1).  Lo interesante es que los cambios solo van a suceder en los 
  //   flancos de subida (cuando se enciende) de una entrada que llamamos 'Clock'.
  //   Tambien , en caso de ser necesario, cuenta con un dato Q' que es la negacion del dato Q.
  //   El problema que surge es que cuando el 'SET' y el 'RESET' estan activos al tiempo y 
  //   hay un flaco de subida del reloj, el sistema comienza a oscilar dando una salida inestable.
endmodule
