// Digital circuit Ejercicio3b.dig as structural Verilog
module Ejercicio3b (
  input  J,
  input  K,
  input  Clock,
  output Q,
  output Q_2
);

  wire nand_1_out, nand_2_out, nand_3_out, nand_4_out, nand_5_out, nand_6_out, nand_7_out, nand_8_out,
       not_1_out, not_2_out, not_3_out;

  nand nand_1 (nand_1_out, Q_2, J);
  nand nand_2 (nand_2_out, K, Q);
  not not_1 (not_1_out, nand_1_out);
  not not_2 (not_2_out, Clock);
  not not_3 (not_3_out, nand_2_out);
  nand nand_3 (nand_3_out, not_1_out, not_2_out);
  nand nand_4 (nand_4_out, not_2_out, not_3_out);
  nand nand_5 (nand_5_out, nand_3_out, nand_6_out);
  nand nand_6 (nand_6_out, nand_5_out, nand_4_out);
  nand nand_7 (nand_7_out, nand_5_out, Clock);
  nand nand_8 (nand_8_out, Clock, nand_6_out);
  nand nand_9 (Q, nand_7_out, Q_2);
  nand nand_10 (Q_2, Q, nand_8_out);

  // Notes on the sheet:
  //   Este circuito funciona de manera  similar al flip-flop RS, salvo que en vez de las entradas 'SET' y 'RESET'
  //    tenemos las entradas 'J' y 'K'.  Pero el cambio mas importante es que aqui, cuando la entrada 'J' y 'K'  
  //   estan activas al tiempo y se da un flanco de subida del 'Clock', el valor no oscila, sino que comienza 
  //   a alternarse entre 0 y 1 para cada flanco de subida del 'Clock'.
endmodule
