// Digital circuit Ejercicio4.dig as structural Verilog
module Ejercicio4 (
  input  EnControl,
  input  Clear,
  input  Set,
  input  Control1,
  input  Control2,
  input  Control3,
  input  Control4,
  input  clk,
  input  EnSave,
  input  Clear_2,
  input  Set_2,
  input  EnOutput,
  input  Clear_3,
  input  Set_3,
  input  Dato1,
  input  Dato2,
  input  Dato3,
  input  Dato4,
  input  Input_Pin1,
  input  Input_Pin2,
  input  Input_Pin3,
  input  Input_Pin4,
  output Save1,
  output Save2,
  output Save3,
  output Save4,
  output Output_Pin1,
  output Output_Pin2,
  output Output_Pin3,
  output Output_Pin4
);

  wire d_ff_as_5_q, d_ff_as_6_q, d_ff_as_7_q, d_ff_as_8_q, d_ff_as_9_q, d_ff_as_10_q, d_ff_as_11_q,
       d_ff_as_12_q, driver_1_out, driver_2_out, driver_3_out, driver_4_out, multiplexer_1_out,
       multiplexer_2_out, multiplexer_3_out, multiplexer_4_out, multiplexer_5_out, multiplexer_6_out,
       multiplexer_7_out, multiplexer_8_out, multiplexer_9_out, multiplexer_10_out, multiplexer_11_out,
       multiplexer_12_out;

  assign driver_1_out = d_ff_as_5_q ? Input_Pin1 : 1'bz;  // Driver driver_1
  Multiplexer multiplexer_1 (.sel(EnSave), .in_0(Save1), .in_1(driver_1_out), .out(multiplexer_1_out));
  D_FF_AS d_ff_as_1 (.Set(Set_2), .D(multiplexer_1_out), .C(clk), .Clr(Clear_2), .Q(Save1));  // open: nQ
  assign driver_2_out = d_ff_as_6_q ? Input_Pin2 : 1'bz;  // Driver driver_2
  Multiplexer multiplexer_2 (.sel(EnSave), .in_0(Save2), .in_1(driver_2_out), .out(multiplexer_2_out));
  D_FF_AS d_ff_as_2 (.Set(Set_2), .D(multiplexer_2_out), .C(clk), .Clr(Clear_2), .Q(Save2));  // open: nQ
  assign driver_3_out = d_ff_as_7_q ? Input_Pin3 : 1'bz;  // Driver driver_3
  Multiplexer multiplexer_3 (.sel(EnSave), .in_0(Save3), .in_1(driver_3_out), .out(multiplexer_3_out));
  D_FF_AS d_ff_as_3 (.Set(Set_2), .D(multiplexer_3_out), .C(clk), .Clr(Clear_2), .Q(Save3));  // open: nQ
  assign driver_4_out = d_ff_as_8_q ? Input_Pin4 : 1'bz;  // Driver driver_4
  Multiplexer multiplexer_4 (.sel(EnSave), .in_0(Save4), .in_1(driver_4_out), .out(multiplexer_4_out));
  D_FF_AS d_ff_as_4 (.Set(Set_2), .D(multiplexer_4_out), .C(clk), .Clr(Clear_2), .Q(Save4));  // open: nQ
  Multiplexer multiplexer_5 (.sel(EnControl), .in_0(d_ff_as_5_q), .in_1(Control1), .out(multiplexer_5_out));
  D_FF_AS d_ff_as_5 (.Set(Set), .D(multiplexer_5_out), .C(clk), .Clr(Clear), .Q(d_ff_as_5_q));  // open: nQ
  Multiplexer multiplexer_6 (.sel(EnControl), .in_0(d_ff_as_6_q), .in_1(Control2), .out(multiplexer_6_out));
  D_FF_AS d_ff_as_6 (.Set(Set), .D(multiplexer_6_out), .C(clk), .Clr(Clear), .Q(d_ff_as_6_q));  // open: nQ
  Multiplexer multiplexer_7 (.sel(EnControl), .in_0(d_ff_as_7_q), .in_1(Control3), .out(multiplexer_7_out));
  D_FF_AS d_ff_as_7 (.Set(Set), .D(multiplexer_7_out), .C(clk), .Clr(Clear), .Q(d_ff_as_7_q));  // open: nQ
  Multiplexer multiplexer_8 (.sel(EnControl), .in_0(d_ff_as_8_q), .in_1(Control4), .out(multiplexer_8_out));
  D_FF_AS d_ff_as_8 (.Set(Set), .D(multiplexer_8_out), .C(clk), .Clr(Clear), .Q(d_ff_as_8_q));  // open: nQ
  Multiplexer multiplexer_9 (.sel(EnOutput), .in_0(d_ff_as_9_q), .in_1(Dato1), .out(multiplexer_9_out));
  D_FF_AS d_ff_as_9 (.Set(Set_3), .D(multiplexer_9_out), .C(clk), .Clr(Clear_3), .Q(d_ff_as_9_q));  // open: nQ
  assign Output_Pin1 = ~d_ff_as_5_q ? d_ff_as_9_q : 1'bz;  // DriverInvSel driverinvsel_1
  Multiplexer multiplexer_10 (.sel(EnOutput), .in_0(d_ff_as_10_q), .in_1(Dato2), .out(multiplexer_10_out));
  D_FF_AS d_ff_as_10 (.Set(Set_3), .D(multiplexer_10_out), .C(clk), .Clr(Clear_3), .Q(d_ff_as_10_q));  // open: nQ
  assign Output_Pin2 = ~d_ff_as_6_q ? d_ff_as_10_q : 1'bz;  // DriverInvSel driverinvsel_2
  Multiplexer multiplexer_11 (.sel(EnOutput), .in_0(d_ff_as_11_q), .in_1(Dato3), .out(multiplexer_11_out));
  D_FF_AS d_ff_as_11 (.Set(Set_3), .D(multiplexer_11_out), .C(clk), .Clr(Clear_3), .Q(d_ff_as_11_q));  // open: nQ
  assign Output_Pin3 = ~d_ff_as_7_q ? d_ff_as_11_q : 1'bz;  // DriverInvSel driverinvsel_3
  Multiplexer multiplexer_12 (.sel(EnOutput), .in_0(d_ff_as_12_q), .in_1(Dato4), .out(multiplexer_12_out));
  D_FF_AS d_ff_as_12 (.Set(Set_3), .D(multiplexer_12_out), .C(clk), .Clr(Clear_3), .Q(d_ff_as_12_q));  // open: nQ
  assign Output_Pin4 = ~d_ff_as_8_q ? d_ff_as_12_q : 1'bz;  // DriverInvSel driverinvsel_4

  // Other names for the same wires on the sheet: Clock = clk; IPin1 = Input_Pin1; IPin2 = Input_Pin2;
  //   IPin3 = Input_Pin3; IPin4 = Input_Pin4; OPin1 = Output_Pin1; OPin2 = Output_Pin2; OPin3 = Output_Pin3;
  //   OPin4 = Output_Pin4

  // Notes on the sheet:
  //   clk: Hz: 10
  //   De manera sencilla, este circuito lo que hace es que cuando se activa una 
  //   de las entradas del registro de control, este envia una señal equivalente a 
  //   un 1 binario hacia un par de buffers mutuamente excluyentes, de modo  
  //   que se habilita la entrada de informacion unicamente a traves del Pin 
  //   asociado a dicha entrada especifica del registro de control para asi, 
  //   ser almacenada, pero se deshabilita la salida de informacion por ese Pin. 
  //   Si la señal del registro de control es un cero, sucede lo contrario
  //   Registro de almacenamiento
  //   Registro de control
  //   Pines
  //   Pins Input
  //   Pins Output
  //   Registro de salida
endmodule
