// Digital circuit Prueba.dig as structural Verilog
module Prueba (
  input  Set,
  input  Reset,
  input  clk,
  output Q,
  output Q_2
);

  RS_FF rs_ff_1 (.S(Set), .C(clk), .R(Reset), .Q(Q), .nQ(Q_2));

  // Notes on the sheet:
  //   clk: Hz: 10
endmodule
